# Fritzing sketch Midterm_1_SmartRoomv2 (saved by Fritzing 0.9.9b)
breadboards: 1

parts:
  U1 = ENCODER_RGB [package=encoder_led_2]
  LED2 = LED - 3mm [color="Blue (505nm)" current=0.030 package="3 mm [THT]"]
  R2 = Resistor [tolerance=±5% resistance=220 package="0805 [SMD]"]
  R3 = Resistor [tolerance=±5% resistance=220 package="0805 [SMD]"]
  OLED_I2C1 = OLED 128x64 I2C Monochrome Display
  Argon1 = Particle Argon
  S1 = Pushbutton [package="[THT]"]
  PIR1 = PIR sensor

nets (from the schematic view):
  N1: U1.B, Argon1.MI
  N2: U1.A, Argon1.MO
  N3: U1.SW, Argon1.SCK
  VDD: U1.+, R3.Pin_0, OLED_I2C1.VDD, Argon1.3.3V, S1.Pin_1, S1.Pin_2, PIR1.VDD
  N4: LED2.cathode, R2.Pin_0
  N5: LED2.anode, Argon1.D4
  GND: R2.Pin_1, R3.Pin_1, OLED_I2C1.GND, Argon1.GND, PIR1.GND
  N6: OLED_I2C1.SDA, Argon1.SDA
  N7: OLED_I2C1.SCK, Argon1.SCL
  N8: Argon1.D3, S1.Pin_3, S1.Pin_4
  N9: Argon1.D5, PIR1.SIG

custom parts:
  ENCODER_RGB: SparkFun RGB rotary Encoder
  Particle Argon: The Argon is a powerful Wi-Fi enabled development board that can act as either a standalone Wi-Fi endpoint or Wi-Fi enabled gateway for Particle Mesh networks. It is based on the Nordic nRF52840 and has built-in battery charging circuitry so it’s easy to connect a Li-Po and deploy your local network in minutes. The Argon is great for connecting existing projects to the Particle Device Cloud or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
  Pushbutton: A generic pushbutton.
